# Fritzing sketch doorbell (saved by Fritzing 0.9.6b)
circuit board: 8.46667cm x 5.64444cm
breadboards: 1

parts:
  Bauteil2 = Arduino Uno (Rev3)
  LED1 = LED - 5mm [color="Red (633nm)" current=0.030 package="5 mm [THT]"]
  LED2 = LED - 5mm [color="Green (560nm)" current=0.030 package="5 mm [THT]"]
  R1 = Resistor [tolerance=±5% resistance=220 package="0402 [SMD]"]
  R2 = Resistor [tolerance=±5% resistance=220 package="0402 [SMD]"]
  U1 = Sharp PC817 [package=THT]
  U2 = Sharp PC817 [package=THT]
  D1 = Diode [package=diode-1n4148]
  R3 = Resistor [tolerance=±5% resistance=1k package="0402 [SMD]"]
  R4 = Resistor [tolerance=±5% resistance=1k package="0402 [SMD]"]
  D2 = Diode [package=diode-1n4148]
  J1 = screw terminal, 4 pins

nets:
  N1: Bauteil2.D8, R2.Pin_1
  N2: Bauteil2.D9_PWM, R1.Pin_1
  N3: Bauteil2.GND, LED1.cathode, LED2.cathode, U1.Pin_3, U2.Pin_3
  N4: Bauteil2.D2, U2.Pin_4
  N5: Bauteil2.D3_PWM, U1.Pin_4
  N6: LED1.anode, R1.Pin_0
  N7: LED2.anode, R2.Pin_0
  N8: U1.Pin_1, D1.C, R4.Pin_0
  N9: U1.Pin_2, D1.A, J1.pin1
  N10: U2.Pin_1, R3.Pin_0, D2.C
  N11: U2.Pin_2, D2.A, J1.pin3
  N12: R3.Pin_1, J1.pin4
  N13: R4.Pin_1, J1.pin2
